// Logisim project trabalho_todo.circ as structural Verilog: 3 circuits, main circuit BD
module BD (
  input  [2:0] R_ADR,
  input  [31:0] RD,
  input  WR,
  input  [2:0] RS1_I,
  input  [2:0] RS2_I,
  input  CLK,
  output [31:0] RS1_O,
  output [31:0] RS2_O
);

  wire demultiplexer_1_out0, demultiplexer_1_out1, demultiplexer_1_out2, demultiplexer_1_out3,
       demultiplexer_1_out4, demultiplexer_1_out5, demultiplexer_1_out6, demultiplexer_1_out7;
  wire [31:0] X0_q, X1_q, X2_q, X3_q, X4_q, X5_q, X6_q, X7_q;

  Demultiplexer #(.select(3)) demultiplexer_1 (
    .out0(demultiplexer_1_out0), .out1(demultiplexer_1_out1), .out2(demultiplexer_1_out2),
    .out3(demultiplexer_1_out3), .out4(demultiplexer_1_out4), .out5(demultiplexer_1_out5),
    .out6(demultiplexer_1_out6), .out7(demultiplexer_1_out7), .in(WR), .sel(R_ADR));
  Register #(.width(32)) X0 (.D(RD), .en(demultiplexer_1_out7), .clk(CLK), .Q(X0_q));  // open: clr
  Register #(.width(32)) X1 (.D(RD), .en(demultiplexer_1_out6), .clk(CLK), .Q(X1_q));  // open: clr
  Register #(.width(32)) X2 (.D(RD), .en(demultiplexer_1_out5), .clk(CLK), .Q(X2_q));  // open: clr
  Register #(.width(32)) X3 (.D(RD), .en(demultiplexer_1_out4), .clk(CLK), .Q(X3_q));  // open: clr
  Register #(.width(32)) X4 (.D(RD), .en(demultiplexer_1_out3), .clk(CLK), .Q(X4_q));  // open: clr
  Register #(.width(32)) X5 (.D(RD), .en(demultiplexer_1_out2), .clk(CLK), .Q(X5_q));  // open: clr
  Register #(.width(32)) X6 (.D(RD), .en(demultiplexer_1_out1), .clk(CLK), .Q(X6_q));  // open: clr
  Register #(.width(32)) X7 (.D(RD), .en(demultiplexer_1_out0), .clk(CLK), .Q(X7_q));  // open: clr
  Multiplexer #(.select(3), .width(32)) multiplexer_1 (
    .in0(X0_q), .in1(X1_q), .in2(X2_q), .in3(X3_q), .in4(X4_q), .in5(X5_q), .in6(X6_q), .in7(X7_q),
    .out(RS1_O), .sel(RS1_I));
  Multiplexer #(.select(3), .width(32)) multiplexer_2 (
    .in0(X0_q), .in1(X1_q), .in2(X2_q), .in3(X3_q), .in4(X4_q), .in5(X5_q), .in6(X6_q), .in7(X7_q),
    .out(RS2_O), .sel(RS2_I));
endmodule

module main (
);

  BD bd_1 ();  // open: R_ADR, RD, WR, RS1_I, RS2_I, CLK, RS1_O, RS2_O
endmodule

module ULA (
);

  Adder #(.width(24)) adder_1 ();  // open: a, b, out, cin, cout
  Subtractor #(.width(24)) subtractor_1 ();  // open: a, b, out, bin, bout
  Shifter #(.width(24)) shifter_1 ();  // open: in, dist, out
  Shifter #(.shift("lr"), .width(24)) shifter_2 ();  // open: in, dist, out
  Multiplexer #(.select(3)) multiplexer_1 ();  // open: in0, in1, in2, in3, in4, in5, in6, in7, out, sel
endmodule
